# Fritzing sketch moisturesensor (saved by Fritzing 0.8.7b)
circuit board: 10.4391cm x 5.16131cm
perfboards: 1

parts:
  R1 = Resistor [tolerance=±10% resistance=100 package=THT]  # not connected
  R2 = Resistor [tolerance=±5% resistance=1k package=THT]
  R3 = Resistor [tolerance=±5% resistance=2.2 package=THT]
  LED1 = LED - 5mm [color="Red (633nm)" package="5 mm [THT]"]
  LED2 = LED - 5mm [color="Green (555nm)" package="5 mm [THT]"]

nets:
  N1: R2.Pin_1, R3.Pin_0, R3.Pin_1, LED2.anode
  N2: LED1.cathode, LED2.cathode
