# Fritzing sketch moisturesensor_w_arduino (saved by Fritzing 0.8.7b)
circuit board: 8.609cm x 5.68914cm
perfboards: 1

parts:
  Part1 = Arduino Uno (Rev3)
  R1 = Resistor [tolerance=±10% resistance=100 package=THT]
  R2 = Resistor [tolerance=±5% resistance=1k package=THT]
  R3 = Resistor [tolerance=±5% resistance=2.2 package=THT]
  LED1 = LED - 5mm [color="Red (633nm)" package="5 mm [THT]"]
  LED2 = LED - 5mm [color="Green (555nm)" package="5 mm [THT]"]

nets:
  N1: Part1.A0, R1.Pin_1
  N2: Part1.D8, Part1.D10_PWM/SS, R2.Pin_0, R2.Pin_1, R3.Pin_0, R3.Pin_1, LED1.anode, LED2.anode
  N3: Part1.GND, LED1.cathode, LED2.cathode
  N4: Part1.D2, R1.Pin_0
